# Fritzing sketch sensor-receiver-design (saved by Fritzing 0.9.10b)

parts:
  Part1 = Arduino Uno (Rev3) - ICSP
  Rx1 = mystery part, 4 pins [chip_label=?]
  Part2 = Jtron 1 Channel Optoisolated Relay Module [package=relay]
  J1 = Piezo Speaker
  BAT1 = 12 battery [package=battery]
  S1 = Reed switch [package=THT]
  S2 = Reed switch [package=THT]
  S3 = Reed switch [package=THT]
  S4 = Reed switch [package=THT]

nets:
  N1: Part1.ICSP_MOSI, Part1.D11_PWM/MOSI, Rx1.pin3
  N2: Part1.D8, S1.pin_2, S3.pin_2, S4.pin_2
  N3: Part1.D13/SCK, Part2.IN1
  GND: Part1.GND, Rx1.pin1, Part2.GND, S1.pin_1, S2.pin_1, S3.pin_1
  5V: Part1.5V, Rx1.pin4, Part2.VCC
  N4: Part2.NO, J1.pin2
  N5: Part2.MAIN, BAT1.+
  N6: J1.pin1, BAT1.-

notes:
  443MHz receiver
  NC reed switches in parallel, triggers if any of them close
  Battery power from obd2 port
  Relay to activate alarm
  120dB piezo alarm siren
  Arduino controller

custom parts:
  12 battery: 12V lead acid type battery, like the Husqvarna YTH2448 12V 35AH battery. This is the mini version 1/4 the size of the actual battery to be closer to typical breadboard parts (around 2in wide rathher than 7in). The pads in pcb are sized to accomidate up to 14ga wire (as these batterys will deliver high currents.)
